# Fritzing sketch Plant Waterer (saved by Fritzing 0.9.3b)
circuit board: 8.46667cm x 5.64444cm
breadboards: 1

parts:
  Particle = Photon
  Part2 = Soil Moisture Sensor
  SRD-05VDC-SL-C = songle relay
  Pump = DC Motor

nets:
  N1: Particle.A0, Part2.SIG
  GND: Particle.GND, Part2.GND, SRD-05VDC-SL-C.GND, Pump.pin_2
  VCC: Particle.VIN, Part2.VCC, SRD-05VDC-SL-C.VCC, SRD-05VDC-SL-C.NC
  N2: Particle.D0, SRD-05VDC-SL-C.COMMON
  N3: SRD-05VDC-SL-C.NO, Pump.pin_1
